# Fritzing sketch licenta (saved by Fritzing 0.9.4)
breadboards: 1

parts:
  M3 = Getriebemotor
  M4 = Getriebemotor
  M5 = Getriebemotor
  M6 = Getriebemotor
  L298N1 = L298N DC motor driver
  BAT1 = BC9VPC [package=bc9vpc]
  BAT2 = BC9VPC [package=bc9vpc]
  A1 = Hanmatek HM305
  MH-ET_LIVE_ESP32_DEVKIT1 = MH-ET LIVE ESP32 DEVKIT 38 pins
  INA1 = INA219 DC Current Sensor Breakout
  Q1 = Basic FET N-Channel [package="D2Pak [SMD]"]
  Q2 = NPN-Transistor [package="TO92 [THT]"]
  R1 = Resistor [tolerance=±5% resistance=10k package="0402 [SMD]"]
  R2 = Resistor [tolerance=±5% resistance=1k package="0402 [SMD]"]
  L1 = Inductor [current=2 package="0805 [SMD]"]
  D1 = Rectifier Diode [part_number=1N4001 package="300 mil [THT]"]
  C1 = Electrolytic Capacitor [capacitance=1000μF package="1010 [SMD, electrolytic]"]
  D2 = Rectifier Diode [part_number=1N4001 package="300 mil [THT]"]

nets:
  N1: M3.pin_1, M4.pin_1, L298N1.OUT4
  N2: M3.pin_2, M4.pin_2, L298N1.OUT3
  N3: M5.pin_1, M6.pin_1, L298N1.OUT2
  N4: M5.pin_2, M6.pin_2, L298N1.OUT1
  N5: L298N1.12V, BAT1.V+, BAT2.V+
  GND: L298N1.GND, BAT1.V-, BAT2.V-, A1.Pin_3, MH-ET_LIVE_ESP32_DEVKIT1.GND, INA1.GND, Q2.E, L1.pin_1, D1.anode, C1.-, C1.+, D2.anode
  5V: L298N1.5V, MH-ET_LIVE_ESP32_DEVKIT1.5V
  N6: L298N1.ENA, MH-ET_LIVE_ESP32_DEVKIT1.IO4
  N7: L298N1.ENB, MH-ET_LIVE_ESP32_DEVKIT1.IO19
  N8: L298N1.IN1, MH-ET_LIVE_ESP32_DEVKIT1.IO16
  N9: L298N1.IN2, MH-ET_LIVE_ESP32_DEVKIT1.IO17
  N10: L298N1.IN3, MH-ET_LIVE_ESP32_DEVKIT1.IO5
  N11: L298N1.IN4, MH-ET_LIVE_ESP32_DEVKIT1.IO18
  N12: A1.Pin_4, INA1.Vin+2, R1.Pin_0
  3V3: MH-ET_LIVE_ESP32_DEVKIT1.3V3, INA1.VCC
  N13: MH-ET_LIVE_ESP32_DEVKIT1.IO32, R2.Pin_0
  N14: MH-ET_LIVE_ESP32_DEVKIT1.IO22, INA1.SCL
  N15: MH-ET_LIVE_ESP32_DEVKIT1.IO21, INA1.SDA
  N16: INA1.Vin-2, Q1.drain
  N17: Q1.source, L1.pin_0, D1.cathode
  N18: Q2.B, R2.Pin_1
  N19: Q2.C, R1.Pin_1

custom parts:
  L298N DC motor driver: 2x DC motor driver with 78M05 positive voltage regulator (7..35 V) L298N: max 46 V, 2 A Set 5 V Enable jumper to enable 5 V regultor (needed for the L298N) and +5 V output at screw terminal or supply external +5 V at screw terminal Set ENA and/or ENB to +5 V to enable motor permanently or supply ENA and/or ENB with PWM signal IN1 and IN2 set rotation directory for motor A (OUT1/OUT2) IN2 and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
  Hanmatek HM305: DC Power Supply 30V5A HM305.
  MH-ET LIVE ESP32 DEVKIT 38 pins: http://mh.nodebb.com/topic/2/mh-et-live-esp32-devkit
  INA219 DC Current Sensor Breakout: INA DC Current Sensor Breakout
